# Fritzing sketch wedding_clock (saved by Fritzing 0.9.3b)
breadboards: 1

parts:
  Part1 = Arduino Uno (Rev3)
  SP1 = SPEAKER [package=pcb_mount_speaker]
  J1 = Basic Servo
  J2 = Basic Servo
  VCC1 = Battery
  U1 = SWITCH_SPDT [package=kps-1290]
  J3 = Screw terminal - 2 pins [package=THT]
  1_MOhm = Resistor [tolerance=±5% resistance=220 package="2512 [SMD]"]
  S1 = Round Pushbutton
  10_kOhm = Resistor [tolerance=±5% resistance=220 package="2512 [SMD]"]
  U2 = RELAY [package=relay-g5q]
  D1 = Diode [package=diode-1n4001]
  U3 = BATTERY-2 [package=battery-aaa]
  DUMMY_BATTERY = BATTERY-2 [package=battery-aaa]
  S2 = SWITCH-MOMENTARY-2 [package=reed_switch_plastic]
  Q1 = NPN-Transistor [package="TO92 [THT]"]
  R1 = Resistor [tolerance=±5% resistance=220 package="2512 [SMD]"]
  J4 = Screw terminal - 2 pins [package=THT]

nets:
  N1: Part1.D9_PWM, J2.pulse
  N2: Part1.D10_PWM/SS, J1.pulse
  N3: Part1.D11_PWM/MOSI, SP1.-
  N4: Part1.D2, J3.pin2, 1_MOhm.Pin_1, S2.2
  N5: Part1.D3_PWM, S1.leg1, 10_kOhm.Pin_1
  N6: Part1.D4, R1.Pin_0
  N7: Part1.5V, 1_MOhm.Pin_0, 10_kOhm.Pin_0, U2.COIL1, D1.C
  GND: Part1.GND, SP1.+, J1.gnd, J2.gnd, VCC1.-, J3.pin1, S1.leg0, S2.1, Q1.B
  VCC: J1.vcc, J2.vcc, U1.P
  N8: VCC1.+, U1.S
  N9: U2.COIL2, D1.A, Q1.E
  N10: U2.MAIN, U3.+1
  N11: U2.NO, DUMMY_BATTERY.+1, J4.pin1
  N12: U3.-1, DUMMY_BATTERY.-1, J4.pin2
  N13: Q1.C, R1.Pin_1
